# Fritzing sketch LDR_controlled_buzzer (saved by Fritzing 0.9.3b)
breadboards: 1

parts:
  Part1 = Arduino Uno (Rev3)
  R1 = Photocell (LDR) [package=THT]
  R2 = Resistor [tolerance=±5% resistance=220 package="1206 [SMD]"]
  J1 = Piezo Speaker

nets:
  N1: Part1.A0, R1.pin_0, R2.Pin_1
  N2: Part1.D11_PWM/MOSI, J1.pin2
  N3: Part1.5V, R1.pin_1
  N4: Part1.GND, R2.Pin_0, J1.pin1
